# Fritzing sketch Rainboth_final (saved by Fritzing 0.9.3b)
breadboards: 1

parts:
  U1 = atmega168 [package=dip]
  LED1 = LED - 5mm [color="Red (633nm)" package="5 mm [THT]"]
  LED2 = LED - 5mm [color="Red (633nm)" package="5 mm [THT]"]
  LED3 = LED - 5mm [color="Red (633nm)" package="5 mm [THT]"]
  LED4 = LED - 5mm [color="Red (633nm)" package="5 mm [THT]"]
  M1 = DC Motor
  R1 = Resistor [tolerance=±5% resistance=220 package=THT]
  R2 = Resistor [tolerance=±5% resistance=220 package=THT]
  R3 = Resistor [tolerance=±5% resistance=220 package=THT]
  R4 = Resistor [tolerance=±5% resistance=220 package=THT]
  J1 = Infrared Proximity Sensor
  IC1 = L293D [package=THT]

nets:
  N1: U1.D1_(TX), J1.GND
  VCC: U1.VCC, J1.Vcc, IC1.+V
  N2: U1.GND#7, R1.Pin_1, R2.Pin_1, R3.Pin_1, R4.Pin_1, J1.Vout, IC1.0V, IC1.+Vmotor
  N3: U1.D9_(PWM), LED3.anode
  N4: U1.D10_(PWM), LED4.anode
  N5: U1.D11_(PWM), LED1.anode
  N6: U1.D12, LED2.anode
  N7: U1.A0, IC1.In_2
  N8: U1.A1, IC1.In_1
  N9: LED1.cathode, R2.Pin_0
  N10: LED2.cathode, R1.Pin_0
  N11: LED3.cathode, R4.Pin_0
  N12: LED4.cathode, R3.Pin_0
  N13: M1.pin_1, IC1.Out_2_(_Controlled_by_Enable_1_)
  N14: M1.pin_2, IC1.Out_1_(_Controlled_by_Enable_1_)
